// Digital circuit boot-rom.dig as structural Verilog
module boot_rom (
  input  [7:0] Addr,
  input  En,
  output [31:0] Out_code
);

  wire [7:0] barrelshifter_1_out;

  BarrelShifter #(.Bits(8), .direction("right")) barrelshifter_1 (
    .in(Addr), .shift(4'b0010), .out(barrelshifter_1_out));
  ROM #(.AddrBits(8), .Bits(8)) rom_1 (.A(barrelshifter_1_out), .sel(En), .D(Out_code[7:0]));
  ROM #(.AddrBits(8), .Bits(8)) rom_2 (.A(barrelshifter_1_out), .sel(En), .D(Out_code[15:8]));
  ROM #(.AddrBits(8), .Bits(8)) rom_3 (.A(barrelshifter_1_out), .sel(En), .D(Out_code[23:16]));
  ROM #(.AddrBits(8), .Bits(8)) rom_4 (.A(barrelshifter_1_out), .sel(En), .D(Out_code[31:24]));

  // Notes on the sheet:
  //   contents of rom_1 (hex, n*v repeats v):
  //   7f,b7,13,93,3,b3,23,13,e3,93,13,93,13,6f
  //   contents of rom_2 (hex, n*v repeats v):
  //   0,0,1,1,c2,80,0,1,48,0,1,1,2
  //   contents of rom_3 (hex, n*v repeats v):
  //   5*0,20,41,11,31
  //   contents of rom_4 (hex, n*v repeats v):
  //   80,40,0,40,4*0,fe
endmodule
