// Digital circuit risc-v-computer.dig as structural Verilog
module risc_v_computer (
  input  CPUClock,
  input  TimerClock,
  input  UartClock,
  input  GPIO_in1,
  input  GPIO_in2,
  input  GPIO_in3,
  input  GPIO_in4,
  input  GPIO_in5,
  input  GPIO_in6,
  input  GPIO_in7,
  input  GPIO_in8,
  input  GPIO_in9,
  input  GPIO_in10,
  input  IICClock,
  input  clk,
  output out_15,
  output [7:0] out_16,
  output [31:0] out_18
);

  wire en_ssd, gpio_out1, gpio_out2, gpio_out3, gpio_out4, gpio_out5, gpio_out6, gpio_out7, gpio_out8,
       gpio_out9, gpio_out10, key_out, MCU_tx, SCL, SDA;
  wire [7:0] byte_ssd;
  wire [23:0] addr_ssd;

  ROM #(.AddrBits(24), .Bits(8)) Program_Rom (.A(addr_ssd), .sel(en_ssd), .D(byte_ssd));
  risc_v_mcu MCU (
    .Clock(CPUClock), .TimerClock(TimerClock), .UartClock(UartClock), .IICClock(IICClock),
    .GPIO_in1(GPIO_in1), .GPIO_in2(GPIO_in2), .GPIO_in3(GPIO_in3), .GPIO_in4(GPIO_in4), .GPIO_in5(GPIO_in5),
    .GPIO_in6(GPIO_in6), .GPIO_in7(GPIO_in7), .GPIO_in8(GPIO_in8), .GPIO_in9(GPIO_in9),
    .GPIO_in10(GPIO_in10), .RX(key_out), .SDA_in(SDA), .ssd_bytein(byte_ssd), .GPIO_1(gpio_out1),
    .GPIO_2(gpio_out2), .GPIO_3(gpio_out3), .GPIO_4(gpio_out4), .GPIO_5(gpio_out5), .GPIO_6(gpio_out6),
    .GPIO_7(gpio_out7), .GPIO_8(gpio_out8), .GPIO_9(gpio_out9), .GPIO_10(gpio_out10), .TX(MCU_tx),
    .SDA_out(SDA), .SCL(SCL), .Addr_ssd(addr_ssd), .ssd_en(en_ssd), .sss(out_18));  // open: sss11
  PullUp pullup_1 (.out(SDA));
  // uart_term uart_term: pin names not known; wires that end beside it: MCU_tx, UartClock, clk, key_out, out_15, out_16
  i2c_random IIC_RANDOM_GENERATER (.SDA(SDA), .SCL(SCL), .Dev_address(7'b0000001), .SDA_out(SDA));  // open: rand
  LED led_1 (.in(gpio_out1));
  LED led_2 (.in(gpio_out2));
  LED led_3 (.in(gpio_out3));
  LED led_4 (.in(gpio_out4));
  LED led_5 (.in(gpio_out5));
  LED led_6 (.in(gpio_out6));
  LED led_7 (.in(gpio_out7));

  // Other names for the same wires on the sheet: cpu_clock = CPUClock; iic_clock = IICClock; Timer_clock = TimerClock;
  //   uart_clock = UartClock

  // Notes on the sheet:
  //   CPUClock: Hz: 50000
  //   TimerClock: Hz: 100
  //   UartClock: Hz: 50000
  //   IICClock: Hz: 5000
  //   contents of Program_Rom (hex, n*v repeats v):
  //   97,7,0,0,93,87,c7,2,93,87,17,0,f3,93,57,30,37,2e,0,0,13,e,8e,80
  //   ,f3,13,e,30,37,1,0,1,ef,0,50,1b,f3,13,45,30,67,80,0,0,ef,0,c0
  //   ,47,73,0,20,30,13,0,0,0,13,0,0,0,13,0,0,0,13,0,0,0,13,0,0,0,ef
  //   ,0,40,46,73,0,20,30,13,0,0,0,13,0,0,0,ef,0,80,46,73,0,20,30,13
  //   ,1,1,ff,13,5,f0,7,23,26,11,0,ef,0,0,35,b7,17,0,2,83,a7,7,e8,63
  //   ,86,7,6,23,24,81,0,37,14,0,2,83,27,84,e7,63,92,7,4,ef,0,80,38
  //   ,13,65,f5,7,ef,0,40,37,93,7,10,0,23,2c,f4,e6,3,24,81,0,37,15,0
  //   ,2,13,5,5,9f,ef,0,80,50,37,6,0,2,83,20,c1,0,13,6,6,6,13,5,40,1f
  //   ,93,5,0,0,13,1,1,1,6f,0,10,0,ef,0,80,34,13,75,5,f8,ef,0,40,33
  //   ,23,2c,4,e6,3,24,81,0,6f,f0,5f,fc,ef,0,0,33,13,75,5,f8,ef,0,c0
  //   ,31,b7,17,0,2,3,a5,c7,e7,13,5,15,0,13,7,70,0,63,4c,a7,0,13,7,5
  //   ,0,93,5,10,0,23,ae,e7,e6,ef,0,80,2b,6f,f0,1f,f9,13,7,10,0,13,5
  //   ,7,0,6f,f0,9f,fe,13,1,1,ff,13,5,a0,0,23,26,11,0,ef,0,0,2f,b7,17
  //   ,0,2,23,a0,a7,e8,ef,0,0,30,37,15,0,2,83,20,c1,0,13,5,45,a0,13
  //   ,1,1,1,6f,0,40,46,13,1,1,ff,13,5,f0,7,23,22,91,0,23,20,21,1,23
  //   ,26,11,0,23,24,81,0,b7,14,0,2,ef,0,c0,24,13,9,80,0,13,5,a0,0,ef
  //   ,0,40,2a,23,a0,a4,e8,13,4,10,0,63,a,5,4,ef,0,80,28,13,65,f5,7
  //   ,ef,0,40,27,93,5,0,0,13,5,40,1f,ef,0,40,7e,ef,0,0,27,13,75,5,f8
  //   ,ef,0,c0,25,13,5,40,1f,93,5,0,0,ef,0,c0,7c,13,5,a0,0,ef,0,0,26
  //   ,23,a0,a4,e8,13,4,10,0,e3,10,5,fc,6f,0,c0,0,83,a7,4,e8,e3,90,7
  //   ,fa,13,5,4,0,93,5,10,0,ef,0,40,1e,13,5,40,1f,93,5,0,0,ef,0,40
  //   ,79,13,5,4,0,93,5,0,0,13,4,14,0,ef,0,80,1c,e3,18,24,fd,6f,f0,1f
  //   ,f7,13,1,1,ff,23,26,11,0,ef,0,0,72,37,6,0,2,93,5,0,0,13,6,6,6
  //   ,13,5,40,1f,ef,0,0,6a,b7,5,0,2,93,85,45,12,13,5,10,0,ef,0,0,21
  //   ,6f,0,0,0,13,6,10,0,13,1,1,fc,93,5,6,0,13,5,6,0,23,2e,11,2,23
  //   ,28,21,3,23,26,31,3,23,24,41,3,23,22,51,3,23,20,61,3,23,2e,71
  //   ,1,23,2c,81,1,23,2c,81,2,23,2a,91,2,ef,0,0,44,13,6,40,6,93,5,20
  //   ,0,13,5,10,0,ef,0,0,43,93,5,0,0,13,5,10,0,ef,0,c0,4c,93,9,5,0
  //   ,b7,1a,0,2,37,1a,0,2,37,1b,0,2,37,1c,0,2,b7,1b,0,2,13,9,a0,0,13
  //   ,85,ca,a1,ef,0,c0,2f,23,26,1,0,ef,0,c0,32,13,4,5,0,93,4,c1,0,13
  //   ,5,80,6,63,4,24,3,ef,0,40,21,13,5,4,0,ef,0,c0,20,23,80,84,0,ef
  //   ,0,80,30,13,4,5,0,93,84,14,0,13,5,80,6,e3,10,24,ff,13,5,8a,a4
  //   ,ef,0,80,2b,13,5,c1,0,ef,0,c0,5,63,8a,a9,0,63,fe,a9,0,13,5,cc
  //   ,a4,ef,0,0,2a,6f,f0,df,f9,13,5,b,a4,ef,0,40,29,6f,f0,1f,f9,13
  //   ,85,8b,a5,ef,0,80,28,6f,f0,5f,f8,13,1,1,ff,23,24,81,0,23,26,11
  //   ,0,13,4,5,0,63,4,6,0,ef,f0,df,fe,13,5,4,0,83,20,c1,0,3,24,81,0
  //   ,13,1,1,1,67,80,0,0,83,47,5,0,13,7,5,0,13,5,0,0,63,86,7,2,93,16
  //   ,25,0,33,5,d5,0,93,87,7,fd,13,7,17,0,13,15,15,0,33,5,f5,0,83,47
  //   ,7,0,13,75,f5,f,e3,90,7,fe,67,80,0,0,67,80,0,0,63,8e,5,0,b7,7
  //   ,0,a0,13,5,f5,ff,3,a7,7,0,b3,95,a5,0,b3,e5,e5,0,23,a0,b7,0,67
  //   ,80,0,0,b7,7,0,a0,23,a0,a7,0,67,80,0,0,37,7,0,a0,13,5,f5,ff,93
  //   ,7,10,0,13,7,47,0,b3,97,a7,0,3,27,7,0,63,8a,5,0,33,67,f7,0,b7
  //   ,7,0,a0,23,a2,e7,0,67,80,0,0,93,c7,f7,ff,33,f7,e7,0,b7,7,0,a0
  //   ,23,a2,e7,0,67,80,0,0,b7,7,0,a0,23,a2,a7,0,67,80,0,0,b7,7,0,a0
  //   ,3,a5,47,0,67,80,0,0,37,7,0,a0,13,5,f5,ff,93,7,10,0,b3,97,a7,0
  //   ,3,25,47,0,33,f5,a7,0,67,80,0,0,b7,7,0,a0,23,a4,7,0,67,80,0,0
  //   ,b7,17,0,2,13,15,25,0,93,87,7,e1,b3,87,a7,0,37,17,0,2,23,a0,b7
  //   ,0,3,25,47,e8,93,7,f0,7f,63,f4,a7,0,67,80,0,0,b7,17,0,0,93,87
  //   ,7,80,33,65,f5,0,23,22,a7,e8,6f,f0,5f,ba,37,17,0,2,83,27,47,e8
  //   ,93,e7,7,8,13,6,5,0,b7,16,0,2,13,85,7,0,23,a4,c6,e8,23,22,f7,e8
  //   ,6f,f0,1f,b8,67,80,0,0,b7,17,0,2,83,a7,87,e8,63,84,7,0,67,80,7
  //   ,0,67,80,0,0,b7,17,0,b0,3,a7,7,0,b7,17,0,2,13,17,27,0,93,87,7
  //   ,e1,b3,87,e7,0,83,a7,7,0,63,84,7,0,67,80,7,0,67,80,0,0,b7,7,0
  //   ,a0,23,82,a7,10,13,87,7,11,83,27,7,0,93,f7,17,0,e3,8c,7,fe,67
  //   ,80,0,0,63,8a,5,2,37,6,0,a0,13,7,6,0,b3,6,b5,0,13,6,46,10,13,7,7
  //   ,11,83,47,5,0,23,0,f6,0,83,27,7,0,93,f7,17,0,e3,8c,7,fe,13,5,15
  //   ,0,e3,14,d5,fe,67,80,0,0,13,8,5,0,63,84,5,6,b7,7,0,c0,37,3,0,a0
  //   ,b7,8,0,40,b3,85,f5,0,13,3,c3,10,93,88,f8,ff,13,5,0,0,6f,0,80
  //   ,1,83,c7,7,0,23,0,f7,0,13,5,15,0,63,84,b6,2,93,87,6,0,93,86,17
  //   ,0,33,87,16,1,3,26,3,0,33,7,e8,0,e3,ee,c7,fc,37,7,0,a0,23,24,f7
  //   ,10,67,80,0,0,93,87,5,0,37,7,0,a0,23,24,f7,10,67,80,0,0,13,5,0,0
  //   ,b7,7,0,c0,6f,f0,df,fd,83,47,5,0,63,88,7,2,b7,6,0,a0,13,87,6,0
  //   ,13,7,7,11,93,86,46,10,13,5,15,0,23,80,f6,0,83,27,7,0,93,f7,17
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endmodule
